// Digital circuit ALU.dig as structural Verilog
module ALU (
  input  [7:0] A,
  input  [7:0] B,
  input  Op,
  output [7:0] Out,
  output C_out
);

  wire [7:0] noter_8_biti_1_out;

  Noter_8_biti noter_8_biti_1 (.A(B), .Sub(Op), .Out(noter_8_biti_1_out));
  Sumator_8_biti sumator_8_biti_1 (.Cin_p(Op), .A(A), .B(noter_8_biti_1_out), .Out(Out), .Cout_p(C_out));
endmodule
