// Digital circuit Counter2.dig as structural Verilog
module Counter2 (
  input  EN,
  input  C,
  input  clr,
  output ovf,
  output [2:0] out
);

  wire mux_2_1_1_out, mux_2_1_2_out, mux_2_1_3_out, sumator_1_bit_1_cout, sumator_1_bit_1_s,
       sumator_1_bit_2_cout, sumator_1_bit_2_s, sumator_1_bit_3_s;

  Registru_1_bit registru_1_bit_1 (.En(EN), .Clk(C), .I(mux_2_1_1_out), .O(out[0]));
  Registru_1_bit registru_1_bit_2 (.En(EN), .Clk(C), .I(mux_2_1_2_out), .O(out[1]));
  Registru_1_bit registru_1_bit_3 (.En(EN), .Clk(C), .I(mux_2_1_3_out), .O(out[2]));
  PullDown pulldown_1 (.out(out[0]));
  PullDown pulldown_2 (.out(out[2]));
  PullDown pulldown_3 (.out(out[1]));
  Sumator_1_bit sumator_1_bit_1 (.A(out[0]), .B(1'b1), .Cin(1'b0), .S(sumator_1_bit_1_s), .Cout(sumator_1_bit_1_cout));
  Sumator_1_bit sumator_1_bit_2 (
    .A(out[1]), .B(1'b0), .Cin(sumator_1_bit_1_cout), .S(sumator_1_bit_2_s), .Cout(sumator_1_bit_2_cout));
  Sumator_1_bit sumator_1_bit_3 (.A(out[2]), .B(1'b0), .Cin(sumator_1_bit_2_cout), .S(sumator_1_bit_3_s), .Cout(ovf));
  Mux_2_1 mux_2_1_1 (.A(sumator_1_bit_1_s), .B(1'b0), .Sel(clr), .Out(mux_2_1_1_out));
  Mux_2_1 mux_2_1_2 (.A(sumator_1_bit_2_s), .B(1'b0), .Sel(clr), .Out(mux_2_1_2_out));
  Mux_2_1 mux_2_1_3 (.A(sumator_1_bit_3_s), .B(1'b0), .Sel(clr), .Out(mux_2_1_3_out));
endmodule
