// Digital circuit Decodificator_2_4.dig as structural Verilog
module Decodificator_2_4 (
  input  A,
  input  B,
  output O1,
  output O2,
  output O3,
  output O4
);

  wire poarta_nand_1_output_nand, poarta_nand_2_output_nand, poarta_nand_3_output_nand,
       poarta_nand_4_output_nand, poarta_not_2_1_out, poarta_not_2_2_out;

  Poarta_Not_2 poarta_not_2_1 (.In(A), .Out(poarta_not_2_1_out));
  Poarta_Not_2 poarta_not_2_2 (.In(B), .Out(poarta_not_2_2_out));
  Poarta_Nand poarta_nand_1 (
    .Input2(poarta_not_2_1_out), .Input1(poarta_not_2_2_out), .Output_Nand(poarta_nand_1_output_nand));
  Poarta_Nand poarta_nand_2 (.Input2(poarta_not_2_1_out), .Input1(B), .Output_Nand(poarta_nand_2_output_nand));
  Poarta_Nand poarta_nand_3 (.Input2(A), .Input1(poarta_not_2_2_out), .Output_Nand(poarta_nand_3_output_nand));
  Poarta_Nand poarta_nand_4 (.Input2(A), .Input1(B), .Output_Nand(poarta_nand_4_output_nand));
  Poarta_Not_2 poarta_not_2_3 (.In(poarta_nand_1_output_nand), .Out(O1));
  Poarta_Not_2 poarta_not_2_4 (.In(poarta_nand_2_output_nand), .Out(O2));
  Poarta_Not_2 poarta_not_2_5 (.In(poarta_nand_3_output_nand), .Out(O3));
  Poarta_Not_2 poarta_not_2_6 (.In(poarta_nand_4_output_nand), .Out(O4));
endmodule
