// Digital circuit Mux_2_1.dig as structural Verilog
module Mux_2_1 (
  input  A,
  input  B,
  input  Sel,
  output Out
);

  wire poarta_not_2_1_out;

  Poarta_Not_2 poarta_not_2_1 (.In(Sel), .Out(poarta_not_2_1_out));
  PFET pfet_1 (.G(Sel), .S(Out), .D(A));
  NFET nfet_1 (.G(poarta_not_2_1_out), .D(A), .S(Out));
  PFET pfet_2 (.G(poarta_not_2_1_out), .S(Out), .D(B));
  NFET nfet_2 (.G(Sel), .D(B), .S(Out));
endmodule
