// Digital circuit Mux_2_1_8biti.dig as structural Verilog
module Mux_2_1_8biti (
  input  Sel,
  input  [7:0] A,
  input  [7:0] B,
  output [7:0] Out
);

  Mux_2_1 mux_2_1_1 (.A(A[0]), .B(B[0]), .Sel(Sel), .Out(Out[0]));
  Mux_2_1 mux_2_1_2 (.A(A[1]), .B(B[1]), .Sel(Sel), .Out(Out[1]));
  Mux_2_1 mux_2_1_3 (.A(A[2]), .B(B[2]), .Sel(Sel), .Out(Out[2]));
  Mux_2_1 mux_2_1_4 (.A(A[3]), .B(B[3]), .Sel(Sel), .Out(Out[3]));
  Mux_2_1 mux_2_1_5 (.A(A[4]), .B(B[4]), .Sel(Sel), .Out(Out[4]));
  Mux_2_1 mux_2_1_6 (.A(A[5]), .B(B[5]), .Sel(Sel), .Out(Out[5]));
  Mux_2_1 mux_2_1_7 (.A(A[6]), .B(B[6]), .Sel(Sel), .Out(Out[6]));
  Mux_2_1 mux_2_1_8 (.A(A[7]), .B(B[7]), .Sel(Sel), .Out(Out[7]));
endmodule
