// Digital circuit Mux_8_1_8biti.dig as structural Verilog
module Mux_8_1_8biti (
  input  [7:0] In0,
  input  [7:0] In1,
  input  [7:0] In2,
  input  [7:0] In3,
  input  [7:0] In4,
  input  [7:0] In5,
  input  [7:0] In6,
  input  [7:0] In7,
  input  [2:0] Sel_3,
  output [7:0] Out
);

  wire [7:0] mux_2_1_8biti_1_out, mux_2_1_8biti_2_out, mux_2_1_8biti_3_out, mux_2_1_8biti_4_out,
       mux_2_1_8biti_5_out, mux_2_1_8biti_6_out;

  Mux_2_1_8biti mux_2_1_8biti_1 (.Sel(Sel_3[0]), .A(In0), .B(In1), .Out(mux_2_1_8biti_1_out));
  Mux_2_1_8biti mux_2_1_8biti_2 (.Sel(Sel_3[0]), .A(In2), .B(In3), .Out(mux_2_1_8biti_2_out));
  Mux_2_1_8biti mux_2_1_8biti_3 (.Sel(Sel_3[0]), .A(In4), .B(In5), .Out(mux_2_1_8biti_3_out));
  Mux_2_1_8biti mux_2_1_8biti_4 (.Sel(Sel_3[0]), .A(In6), .B(In7), .Out(mux_2_1_8biti_4_out));
  Mux_2_1_8biti mux_2_1_8biti_5 (
    .Sel(Sel_3[1]), .A(mux_2_1_8biti_1_out), .B(mux_2_1_8biti_2_out), .Out(mux_2_1_8biti_5_out));
  Mux_2_1_8biti mux_2_1_8biti_6 (
    .Sel(Sel_3[1]), .A(mux_2_1_8biti_3_out), .B(mux_2_1_8biti_4_out), .Out(mux_2_1_8biti_6_out));
  Mux_2_1_8biti mux_2_1_8biti_7 (.Sel(Sel_3[2]), .A(mux_2_1_8biti_5_out), .B(mux_2_1_8biti_6_out), .Out(Out));
endmodule
