// Digital circuit Noter_8_biti.dig as structural Verilog
module Noter_8_biti (
  input  [7:0] A,
  input  Sub,
  output [7:0] Out
);

  Poarta_Xor poarta_xor_1 (.A(Sub), .B(A[0]), .Out(Out[0]));
  Poarta_Xor poarta_xor_2 (.A(Sub), .B(A[1]), .Out(Out[1]));
  Poarta_Xor poarta_xor_3 (.A(Sub), .B(A[2]), .Out(Out[2]));
  Poarta_Xor poarta_xor_4 (.A(Sub), .B(A[3]), .Out(Out[3]));
  Poarta_Xor poarta_xor_5 (.A(Sub), .B(A[4]), .Out(Out[4]));
  Poarta_Xor poarta_xor_6 (.A(Sub), .B(A[5]), .Out(Out[5]));
  Poarta_Xor poarta_xor_7 (.A(Sub), .B(A[6]), .Out(Out[6]));
  Poarta_Xor poarta_xor_8 (.A(Sub), .B(A[7]), .Out(Out[7]));
endmodule
