// Digital circuit Numarator_1_bit.dig as structural Verilog
module Numarator_1_bit (
  input  Reset,
  input  Clk,
  input  Count_En,
  input  Cin,
  output O,
  output Cout
);

  wire poarta_nand_1_output_nand, poarta_not_2_1_out, poarta_not_2_2_out, registru_1_bit_1_o,
       sumator_1_bit_1_s;

  Poarta_Nand poarta_nand_1 (.Input2(Reset), .Input1(sumator_1_bit_1_s), .Output_Nand(poarta_nand_1_output_nand));
  Poarta_Not_2 poarta_not_2_1 (.In(poarta_nand_1_output_nand), .Out(poarta_not_2_1_out));
  Poarta_Not_2 poarta_not_2_2 (.In(Clk), .Out(poarta_not_2_2_out));
  Registru_1_bit registru_1_bit_1 (
    .En(Count_En), .Clk(poarta_not_2_2_out), .I(poarta_not_2_1_out), .O(registru_1_bit_1_o));
  Registru_1_bit registru_1_bit_2 (.En(Count_En), .Clk(Clk), .I(registru_1_bit_1_o), .O(O));
  Sumator_1_bit sumator_1_bit_1 (.A(O), .B(1'b0), .Cin(Cin), .S(sumator_1_bit_1_s), .Cout(Cout));
endmodule
