// Digital circuit Numarator_3_biti.dig as structural Verilog
module Numarator_3_biti (
  input  Reset,
  input  Count_En,
  input  Cin,
  input  Clk,
  output [2:0] Out
);

  wire numarator_1_bit_1_cout, numarator_1_bit_2_cout;

  Numarator_1_bit numarator_1_bit_1 (
    .Reset(Reset), .Count_En(Count_En), .Clk(Clk), .Cin(Cin), .O(Out[0]), .Cout(numarator_1_bit_1_cout));
  Numarator_1_bit numarator_1_bit_2 (
    .Reset(Reset), .Clk(Clk), .Count_En(Count_En), .Cin(numarator_1_bit_1_cout), .O(Out[1]),
    .Cout(numarator_1_bit_2_cout));
  Numarator_1_bit numarator_1_bit_3 (
    .Reset(Reset), .Clk(Clk), .Count_En(Count_En), .Cin(numarator_1_bit_2_cout), .O(Out[2]));  // open: Cout
endmodule
