// Digital circuit PC_8_biti.dig as structural Verilog
module PC_8_biti (
  input  [7:0] Din,
  input  Count,
  input  LD_C,
  input  Clk,
  output [7:0] O
);

  wire poarta_nor_1_c, poarta_not_2_1_out;
  wire [7:0] mux_2_1_8biti_1_out, sumator_8_biti_1_out;

  Poarta_Nor poarta_nor_1 (.A(Count), .B(LD_C), .C(poarta_nor_1_c));
  Registru_8_biti registru_8_biti_1 (.En(poarta_not_2_1_out), .Clk(Clk), .I(mux_2_1_8biti_1_out), .Out(O));
  Poarta_Not_2 poarta_not_2_1 (.In(poarta_nor_1_c), .Out(poarta_not_2_1_out));
  Sumator_8_biti sumator_8_biti_1 (.Cin_p(1'b0), .A(O), .B(8'h1), .Out(sumator_8_biti_1_out));  // open: Cout_p
  Mux_2_1_8biti mux_2_1_8biti_1 (.Sel(LD_C), .A(sumator_8_biti_1_out), .B(Din), .Out(mux_2_1_8biti_1_out));
endmodule
