// Digital circuit Poarta_Nand.dig as structural Verilog
module Poarta_Nand (
  input  Input2,
  input  Input1,
  output Output_Nand
);

  wire nfet_1_s;

  PFET pfet_1 (.G(Input1), .S(1'b1), .D(Output_Nand));
  PFET pfet_2 (.G(Input2), .S(1'b1), .D(Output_Nand));
  NFET nfet_1 (.G(Input1), .D(Output_Nand), .S(nfet_1_s));
  NFET nfet_2 (.G(Input2), .D(nfet_1_s), .S(1'b0));
endmodule
