// Digital circuit Poarta_Nor.dig as structural Verilog
module Poarta_Nor (
  input  A,
  input  B,
  output C
);

  wire pfet_1_d;

  PFET pfet_1 (.G(A), .S(1'b1), .D(pfet_1_d));
  PFET pfet_2 (.G(B), .S(pfet_1_d), .D(C));
  NFET nfet_1 (.G(A), .D(C), .S(1'b0));
  NFET nfet_2 (.G(B), .D(1'b0), .S(C));
endmodule
