// Digital circuit Poarta_Not_1.dig as structural Verilog
module Poarta_Not_1 (
  input  Input1,
  output Output_Not
);

  Poarta_Nand poarta_nand_1 (.Input2(Input1), .Input1(Input1), .Output_Nand(Output_Not));
endmodule
