// Digital circuit Poarta_Not_2.dig as structural Verilog
module Poarta_Not_2 (
  input  In,
  output Out
);

  PFET pfet_1 (.G(In), .S(1'b1), .D(Out));
  NFET nfet_1 (.G(In), .D(Out), .S(1'b0));
endmodule
