// Digital circuit Poarta_Xor.dig as structural Verilog
module Poarta_Xor (
  input  A,
  input  B,
  output Out
);

  wire nfet_1_s, pfet_1_d, poarta_not_2_1_out, poarta_not_2_2_out;

  PFET pfet_1 (.G(poarta_not_2_1_out), .S(1'b1), .D(pfet_1_d));
  PFET pfet_2 (.G(A), .S(pfet_1_d), .D(Out));
  NFET nfet_1 (.G(poarta_not_2_1_out), .D(Out), .S(nfet_1_s));
  NFET nfet_2 (.G(A), .D(nfet_1_s), .S(1'b0));
  Poarta_Not_2 poarta_not_2_1 (.In(A), .Out(poarta_not_2_1_out));
  Poarta_Not_2 poarta_not_2_2 (.In(B), .Out(poarta_not_2_2_out));
  PFET pfet_3 (.G(poarta_not_2_2_out), .S(pfet_1_d), .D(1'b1));
  PFET pfet_4 (.G(B), .S(Out), .D(pfet_1_d));
  NFET nfet_3 (.G(B), .D(nfet_1_s), .S(Out));
  NFET nfet_4 (.G(poarta_not_2_2_out), .D(1'b0), .S(nfet_1_s));
endmodule
