// Digital circuit Procesor1.dig as structural Verilog
module Procesor1 (
  input  clk
);

  wire PC_p4, PC_p5;
  wire [2:0] numarator_3_biti_1_out;
  wire [3:0] driver_6_out;
  wire [7:0] A_out, alu_1_out, B_out, C_out, IN_out, IR_out, MAR_out, PC_p1, RAM_d;
  wire [19:0] rom_1_d;
  wire [19:7] undriven;

  // Registru_8_biti PC: pin names not known; wires that end beside it: PC_p1, clk, PC_p1, PC_p4, PC_p5
  Registru_8_biti MAR (.Clk(clk), .I(PC_p1), .Out(MAR_out));  // open: En
  Registru_8_biti IR (.Clk(clk), .I(PC_p1), .Out(IR_out));  // open: En
  Registru_8_biti A (.Clk(clk), .I(PC_p1), .Out(A_out));  // open: En
  Registru_8_biti B (.Clk(clk), .I(PC_p1), .Out(B_out));  // open: En
  Registru_8_biti C (.Clk(clk), .I(alu_1_out), .Out(C_out));  // open: En
  Registru_8_biti IN (.Clk(clk), .Out(IN_out));  // open: En, I
  Registru_8_biti OUT (.Clk(clk), .I(PC_p1));  // open: En, Out
  Numarator_3_biti numarator_3_biti_1 (
    .Reset(1'b1), .Count_En(1'b1), .Cin(1'b1), .Clk(clk), .Out(numarator_3_biti_1_out));
  Driver driver_1 (.in(PC_p4), .out(PC_p1[0]));  // open: en
  Driver #(.Bits(8)) driver_2 (.in(A_out), .out(PC_p1));  // open: en
  Driver #(.Bits(8)) driver_3 (.in(B_out), .out(PC_p1));  // open: en
  Driver #(.Bits(8)) driver_4 (.in(C_out), .out(PC_p1));  // open: en
  Driver #(.Bits(8)) driver_5 (.in(IN_out), .out(PC_p1));  // open: en
  Driver #(.Bits(4)) driver_6 (.in(IR_out[3:0]), .out(driver_6_out));  // open: en
  RAMDualPort #(.AddrBits(8), .Bits(8)) RAM (.A(MAR_out), .Din(PC_p1), .str(PC_p5), .C(clk), .ld(1'b1), .D(RAM_d));
  Driver #(.Bits(8)) driver_7 (.in({4'b0000, driver_6_out}), .out(PC_p1));  // open: en
  ROM #(.AddrBits(20), .Bits(8)) rom_1 (
    .A({undriven, numarator_3_biti_1_out, IR_out[7:4]}), .sel(1'b1), .D(rom_1_d[7:0]));
  Driver #(.Bits(8)) driver_8 (.in(RAM_d), .out(PC_p1));  // open: en
  ALU alu_1 (.A(A_out), .B(B_out), .Out(alu_1_out), .C_out(undriven[7]));  // open: Op
  // Pins of 1 and 8 bits meet at PC_p1
  // Pins of 8 and 20 bits meet at {undriven, numarator_3_biti_1_out, IR_out[7:4]}
  // Pins of 8 and 20 bits meet at rom_1_d
endmodule
