// Digital circuit Procesor2.dig as structural Verilog
module Procesor2 (
  input  clk
);

  wire A_en, alu_1_c_out, B_en, C_en, CLC, Count, Flags, In_en, IR_en, Ld, ld_count, Mar_en, Out_en, Str, X;
  wire [2:0] Bus, counter_1_out, OPC;
  wire [7:0] A_out, alu_1_out, B_out, C_out, counterpreset_1_out, IN_out, IR_out, keyboard_1_d, MAR_out,
       Memorie_RAM_d, mux_8_1_8biti_1_out, OUT_out;
  wire [7:7] registru_1_bit_clr_1_o;
  wire [14:0] ROM_Iesire_d;
  wire [15:8] keyboard_1_d_2;

  Keyboard keyboard_1 (.C(clk), .en(1'b1), .D({keyboard_1_d_2, keyboard_1_d}));  // open: av
  Counter #(.Bits(3)) counter_1 (.en(1'b1), .C(clk), .clr(CLC), .out(counter_1_out));  // open: ovf
  RAMDualPort #(.AddrBits(8), .isProgramMemory("true"), .Bits(8)) Memorie_RAM (
    .A(MAR_out), .Din(mux_8_1_8biti_1_out), .str(Str), .C(clk), .ld(Ld), .D(Memorie_RAM_d));
  ALU alu_1 (.A(A_out), .B(B_out), .Op(OPC[2]), .Out(alu_1_out), .C_out(alu_1_c_out));
  PullDown pulldown_1 (.out(OPC[2]));
  Registru_1_bit_clr registru_1_bit_clr_1 (
    .En(Flags), .Clk(clk), .I(alu_1_c_out), .Clr(CLC), .O(registru_1_bit_clr_1_o[7]));
  Registru_8_biti MAR (.En(Mar_en), .Clk(clk), .I(mux_8_1_8biti_1_out), .Out(MAR_out));
  Registru_8_biti A (.En(A_en), .Clk(clk), .I(mux_8_1_8biti_1_out), .Out(A_out));
  Registru_8_biti B (.En(B_en), .Clk(clk), .I(mux_8_1_8biti_1_out), .Out(B_out));
  Registru_8_biti C (.En(C_en), .Clk(clk), .I(mux_8_1_8biti_1_out), .Out(C_out));
  Registru_8_biti IN (.En(In_en), .Clk(clk), .I(keyboard_1_d), .Out(IN_out));
  Registru_8_biti OUT (.En(Out_en), .Clk(clk), .I(mux_8_1_8biti_1_out), .Out(OUT_out));
  Registru_8_biti IR (.En(IR_en), .Clk(clk), .I(mux_8_1_8biti_1_out), .Out(IR_out));
  PullDown pulldown_2 (.out(Flags));
  CounterPreset #(.Bits(8)) counterpreset_1 (
    .en(Count), .C(clk), .dir(1'b0), .in(mux_8_1_8biti_1_out), .ld(ld_count), .clr(1'b0),
    .out(counterpreset_1_out));  // open: ovf
  Mux_8_1_8biti mux_8_1_8biti_1 (
    .In0(Memorie_RAM_d), .In1(counterpreset_1_out), .In2(A_out), .In3(B_out), .In4(C_out), .In5(IN_out),
    .In6(alu_1_out), .In7(IR_out), .Sel_3(Bus), .Out(mux_8_1_8biti_1_out));
  ROM #(.AddrBits(8), .Bits(20)) Rom_Procesor (
    .A({registru_1_bit_clr_1_o[7], counter_1_out, IR_out[7:4]}), .sel(1'b1),
    .D({Str, Ld, Bus, Mar_en, Count, ld_count, A_en, B_en, C_en, In_en, Out_en, IR_en, Flags, OPC, CLC, X}));
  ROM #(.AddrBits(8), .Bits(15)) ROM_Iesire (.A(OUT_out), .sel(1'b1), .D(ROM_Iesire_d));
  LED led_1 (.in(ROM_Iesire_d[0]));
  LED led_2 (.in(ROM_Iesire_d[1]));
  LED led_3 (.in(ROM_Iesire_d[2]));
  LED led_4 (.in(ROM_Iesire_d[3]));
  LED led_5 (.in(ROM_Iesire_d[4]));
  LED led_6 (.in(ROM_Iesire_d[5]));
  LED led_7 (.in(ROM_Iesire_d[6]));
  LED led_8 (.in(ROM_Iesire_d[7]));
  LED led_9 (.in(ROM_Iesire_d[8]));
  LED led_10 (.in(ROM_Iesire_d[9]));
  LED led_11 (.in(ROM_Iesire_d[10]));
  LED led_12 (.in(ROM_Iesire_d[11]));
  LED led_13 (.in(ROM_Iesire_d[12]));
  LED led_14 (.in(ROM_Iesire_d[13]));
  LED led_15 (.in(ROM_Iesire_d[14]));

  // Notes on the sheet:
  //   Rom_Procesor loads rom_content
  //   ROM_Iesire loads rom_output
endmodule
