// Digital circuit Procesor3.dig as structural Verilog
module Procesor3 (
);

  wire A_en, B_en, C_en, CLC, Count, Flags, In_en, IR_en, Ld, ld_count, Mar_en, Out_en, Str, X;
  wire [2:0] Bus, OPC;

  RAMDualPort #(.AddrBits(4), .Bits(8)) ramdualport_1 ();  // open: A, Din, str, C, ld, D
  Register #(.Bits(8)) Mar ();  // open: D, C, en, Q
  CounterPreset #(.Bits(8)) PC ();  // open: en, C, dir, in, ld, clr, out, ovf
  Register #(.Bits(8)) A ();  // open: D, C, en, Q
  Register #(.Bits(8)) B ();  // open: D, C, en, Q
  Register #(.Bits(8)) c ();  // open: D, C, en, Q
  Register #(.Bits(8)) In ();  // open: D, C, en, Q
  Register #(.Bits(8)) Out ();  // open: D, C, en, Q
  Register #(.Bits(8)) IR ();  // open: D, C, en, Q
  Mux_8_1_8biti mux_8_1_8biti_1 ();  // open: In0, In1, In2, In3, In4, In5, In6, In7, Sel_3, Out
  ROM #(.AddrBits(8), .Bits(20)) ROM_procesor (.D({Str, Ld, Bus, Mar_en, Count, ld_count, A_en, B_en, C_en, In_en, Out_en, IR_en, Flags, OPC, CLC, X}));  // open: A, sel
  ROM #(.AddrBits(8), .Bits(15)) ROM_output ();  // open: A, sel, D
endmodule
