// Digital circuit Procesor_final.dig as structural Verilog
module Procesor_final (
  input  CLK,
  input  [7:0] Tastatura_Numerica
);

  wire A1, A2, A3, A_en, alu_1_c_out, B1, B2, B3, B_en, C1, C2, C3, C_en, CLC, Count, D1, D2, D3, E1, E2, E3,
       F1, F2, F3, FLAGS, Flags_t, G1, G2, G3, In_en, IR_en, Ld, ld_count, Mar_en, Out_en,
       poarta_not_2_1_out, Str, X;
  wire [2:0] Bus, counter_1_out, OPC;
  wire [3:0] IR_out, OPCODE2;
  wire [7:0] A_out, Alu_out, B_out, Bus_in, C_out, In_out, Mar_out, Out_out, PC_out, Ram_out;

  Registru_8_biti IN (.En(In_en), .Clk(CLK), .I(Tastatura_Numerica), .Out(In_out));
  Registru_8_biti OUT (.En(Out_en), .Clk(CLK), .I(Bus_in), .Out(Out_out));
  PullDown #(.Bits(8)) pulldown_1 (.out(In_out));
  // Probe on Tastatura_Numerica
  RAMDualPort #(.AddrBits(8), .Bits(8)) Mem_RAM (.A(Mar_out), .Din(Bus_in), .str(Str), .C(CLK), .ld(Ld), .D(Ram_out));
  Registru_8_biti B (.En(B_en), .Clk(CLK), .I(Bus_in), .Out(B_out));
  Registru_8_biti A (.En(A_en), .Clk(CLK), .I(Bus_in), .Out(A_out));
  Registru_8_biti C (.En(C_en), .Clk(CLK), .I(Bus_in), .Out(C_out));
  PullDown #(.Bits(8)) pulldown_2 (.out(A_out));
  PullDown #(.Bits(8)) pulldown_3 (.out(B_out));
  PullDown #(.Bits(8)) pulldown_4 (.out(C_out));
  ALU alu_1 (.A(A_out), .B(B_out), .Op(OPC[0]), .Out(Alu_out), .C_out(alu_1_c_out));
  Mux_8_1_8biti mux_8_1_8biti_1 (
    .In0(Ram_out), .In1(PC_out), .In2(A_out), .In3(B_out), .In4(C_out), .In5(In_out), .In6(Alu_out),
    .In7({4'b0000, IR_out}), .Sel_3(Bus), .Out(Bus_in));
  PullDown #(.Bits(8)) pulldown_5 (.out(Bus_in));
  // Probe on Bus_in
  Registru_1_bit registru_1_bit_1 (.En(Flags_t), .Clk(CLK), .I(alu_1_c_out), .O(FLAGS));
  // Probe on Bus_in
  PC_8_biti pc_8_biti_1 (.Din(Bus_in), .Count(Count), .LD_C(ld_count), .Clk(CLK), .O(PC_out));
  Registru_8_biti MAR (.En(Mar_en), .Clk(CLK), .I(Bus_in), .Out(Mar_out));
  // Probe on Bus_in
  Registru_8_biti IR (.En(IR_en), .Clk(CLK), .I(Bus_in), .Out({OPCODE2, IR_out}));
  PullDown #(.Bits(8)) pulldown_6 (.out(PC_out));
  PullDown #(.Bits(8)) pulldown_7 (.out(Out_out));
  ROM #(.AddrBits(8), .Bits(21)) ROM_Iesire (
    .A(Out_out), .sel(1'b1),
    .D({G3, F3, E3, D3, C3, B3, A3, G2, F2, E2, D2, C2, B2, A2, G1, F1, E1, D1, C1, B1, A1}));
  // Probe on Mar_out
  PullDown #(.Bits(4)) pulldown_8 (.out(OPCODE2));
  Poarta_Not_2 poarta_not_2_1 (.In(CLK), .Out(poarta_not_2_1_out));
  Counter #(.Bits(3)) counter_1 (.en(1'b1), .C(poarta_not_2_1_out), .clr(CLC), .out(counter_1_out));  // open: ovf
  PullDown pulldown_9 (.out(FLAGS));
  LED led_1 (.in(F3));
  LED led_2 (.in(E3));
  ROM #(.AddrBits(8), .Bits(20)) Rom_Procesor (
    .A({FLAGS, counter_1_out, OPCODE2}), .sel(1'b1),
    .D({Str, Ld, Bus, Mar_en, Count, ld_count, A_en, B_en, C_en, In_en, Out_en, IR_en, Flags_t, OPC, CLC, X}));
  LED led_3 (.in(A3));
  LED led_4 (.in(G3));
  LED led_5 (.in(D3));
  // Probe on {Str, Ld, Bus, Mar_en, Count, ld_count, A_en, B_en, C_en, In_en, Out_en, IR_en, Flags_t, OPC, CLC, X}
  LED led_6 (.in(B3));
  LED led_7 (.in(C3));
  // Probe on Bus
  LED led_8 (.in(F2));
  LED led_9 (.in(E2));
  LED led_10 (.in(A2));
  LED led_11 (.in(G2));
  LED led_12 (.in(D2));
  LED led_13 (.in(B2));
  LED led_14 (.in(C2));
  LED led_15 (.in(F1));
  LED led_16 (.in(E1));
  LED led_17 (.in(A1));
  LED led_18 (.in(B1));
  LED led_19 (.in(G1));
  LED led_20 (.in(C1));
  LED led_21 (.in(D1));

  // Notes on the sheet:
  //   ROM_Iesire loads rom_output.hex
  //   Rom_Procesor loads rom_10_mai.hex
endmodule
