// Digital circuit Procesor_final_2.dig as structural Verilog
module Procesor_final_2 (
);

  Registru_8_biti MAR ();  // open: En, Clk, I, Out
  PC_8_biti PC_8 ();  // open: Din, Count, LD_C, Clk, O
  Registru_8_biti A ();  // open: En, Clk, I, Out
  Registru_8_biti B ();  // open: En, Clk, I, Out
  Registru_8_biti C ();  // open: En, Clk, I, Out
  Registru_8_biti IN ();  // open: En, Clk, I, Out
  Registru_8_biti OUT ();  // open: En, Clk, I, Out
  Registru_8_biti IR ();  // open: En, Clk, I, Out
  Mux_8_1_8biti mux_8_1_8biti_1 ();  // open: In0, In1, In2, In3, In4, In5, In6, In7, Sel_3, Out
endmodule
