// Digital circuit Registru_1_bit.dig as structural Verilog
module Registru_1_bit (
  input  En,
  input  Clk,
  input  I,
  output O
);

  wire poarta_nand_1_output_nand, poarta_nand_2_output_nand, poarta_nand_3_output_nand,
       poarta_nand_4_output_nand, poarta_nand_5_output_nand, poarta_nand_6_output_nand,
       poarta_nand_7_output_nand, poarta_nand_9_output_nand, poarta_not_2_1_out, poarta_not_2_2_out,
       poarta_not_2_3_out;

  Poarta_Nand poarta_nand_1 (.Input2(En), .Input1(Clk), .Output_Nand(poarta_nand_1_output_nand));
  Poarta_Not_2 poarta_not_2_1 (.In(poarta_nand_1_output_nand), .Out(poarta_not_2_1_out));
  Poarta_Not_2 poarta_not_2_2 (.In(I), .Out(poarta_not_2_2_out));
  Poarta_Nand poarta_nand_2 (.Input2(I), .Input1(poarta_nand_1_output_nand), .Output_Nand(poarta_nand_2_output_nand));
  Poarta_Nand poarta_nand_3 (
    .Input2(poarta_nand_1_output_nand), .Input1(poarta_not_2_2_out), .Output_Nand(poarta_nand_3_output_nand));
  Poarta_Nand poarta_nand_4 (
    .Input2(poarta_nand_2_output_nand), .Input1(poarta_nand_5_output_nand),
    .Output_Nand(poarta_nand_4_output_nand));
  Poarta_Nand poarta_nand_5 (
    .Input2(poarta_nand_4_output_nand), .Input1(poarta_nand_3_output_nand),
    .Output_Nand(poarta_nand_5_output_nand));
  Poarta_Not_2 poarta_not_2_3 (.In(poarta_nand_4_output_nand), .Out(poarta_not_2_3_out));
  Poarta_Nand poarta_nand_6 (
    .Input2(poarta_nand_4_output_nand), .Input1(poarta_not_2_1_out), .Output_Nand(poarta_nand_6_output_nand));
  Poarta_Nand poarta_nand_7 (
    .Input2(poarta_not_2_1_out), .Input1(poarta_not_2_3_out), .Output_Nand(poarta_nand_7_output_nand));
  Poarta_Nand poarta_nand_8 (.Input2(poarta_nand_6_output_nand), .Input1(poarta_nand_9_output_nand), .Output_Nand(O));
  Poarta_Nand poarta_nand_9 (.Input2(O), .Input1(poarta_nand_7_output_nand), .Output_Nand(poarta_nand_9_output_nand));
endmodule
