// Digital circuit Registru_1_bit_clr.dig as structural Verilog
module Registru_1_bit_clr (
  input  En,
  input  Clk,
  input  I,
  input  Clr,
  output O
);

  wire poarta_nand_1_output_nand, poarta_nand_2_output_nand, poarta_nand_3_output_nand,
       poarta_nand_4_output_nand, poarta_nand_5_output_nand, poarta_nor_1_c, poarta_not_2_1_out,
       poarta_not_2_2_out, poarta_not_2_3_out, poarta_not_2_4_out, poarta_not_2_5_out;

  Poarta_Nor poarta_nor_1 (.A(Clr), .B(En), .C(poarta_nor_1_c));
  Poarta_Not_2 poarta_not_2_1 (.In(Clr), .Out(poarta_not_2_1_out));
  Poarta_Not_2 poarta_not_2_2 (.In(poarta_nor_1_c), .Out(poarta_not_2_2_out));
  Poarta_Nand poarta_nand_1 (.Input2(I), .Input1(poarta_not_2_1_out), .Output_Nand(poarta_nand_1_output_nand));
  Poarta_Nand poarta_nand_2 (.Input2(poarta_not_2_2_out), .Input1(Clk), .Output_Nand(poarta_nand_2_output_nand));
  Poarta_Not_2 poarta_not_2_3 (.In(poarta_nand_1_output_nand), .Out(poarta_not_2_3_out));
  Poarta_Not_2 poarta_not_2_4 (.In(poarta_nand_2_output_nand), .Out(poarta_not_2_4_out));
  Poarta_Not_2 poarta_not_2_5 (.In(poarta_not_2_3_out), .Out(poarta_not_2_5_out));
  Poarta_Nand poarta_nand_3 (
    .Input2(poarta_not_2_4_out), .Input1(poarta_not_2_5_out), .Output_Nand(poarta_nand_3_output_nand));
  Poarta_Nand poarta_nand_4 (
    .Input2(poarta_not_2_3_out), .Input1(poarta_not_2_4_out), .Output_Nand(poarta_nand_4_output_nand));
  Poarta_Nand poarta_nand_5 (.Input2(O), .Input1(poarta_nand_3_output_nand), .Output_Nand(poarta_nand_5_output_nand));
  Poarta_Nand poarta_nand_6 (.Input2(poarta_nand_4_output_nand), .Input1(poarta_nand_5_output_nand), .Output_Nand(O));
endmodule
