// Digital circuit Registru_8_biti.dig as structural Verilog
module Registru_8_biti (
  input  En,
  input  Clk,
  input  [7:0] I,
  output [7:0] Out
);

  Registru_1_bit registru_1_bit_1 (.En(En), .Clk(Clk), .I(I[0]), .O(Out[0]));
  Registru_1_bit registru_1_bit_2 (.En(En), .Clk(Clk), .I(I[1]), .O(Out[1]));
  Registru_1_bit registru_1_bit_3 (.En(En), .Clk(Clk), .I(I[2]), .O(Out[2]));
  Registru_1_bit registru_1_bit_4 (.En(En), .Clk(Clk), .I(I[3]), .O(Out[3]));
  Registru_1_bit registru_1_bit_5 (.En(En), .Clk(Clk), .I(I[4]), .O(Out[4]));
  Registru_1_bit registru_1_bit_6 (.En(En), .Clk(Clk), .I(I[5]), .O(Out[5]));
  Registru_1_bit registru_1_bit_7 (.En(En), .Clk(Clk), .I(I[6]), .O(Out[6]));
  Registru_1_bit registru_1_bit_8 (.En(En), .Clk(Clk), .I(I[7]), .O(Out[7]));
endmodule
