// Digital circuit Sumator_1_bit.dig as structural Verilog
module Sumator_1_bit (
  input  A,
  input  B,
  input  Cin,
  output S,
  output Cout
);

  wire poarta_nand_1_output_nand, poarta_nand_2_output_nand, poarta_not_2_1_out, poarta_not_2_2_out,
       poarta_xor_1_out;

  Poarta_Xor poarta_xor_1 (.A(A), .B(B), .Out(poarta_xor_1_out));
  Poarta_Nand poarta_nand_1 (.Input2(A), .Input1(B), .Output_Nand(poarta_nand_1_output_nand));
  Poarta_Nand poarta_nand_2 (.Input2(Cin), .Input1(poarta_xor_1_out), .Output_Nand(poarta_nand_2_output_nand));
  Poarta_Not_2 poarta_not_2_1 (.In(poarta_nand_1_output_nand), .Out(poarta_not_2_1_out));
  Poarta_Not_2 poarta_not_2_2 (.In(poarta_nand_2_output_nand), .Out(poarta_not_2_2_out));
  Poarta_Xor poarta_xor_2 (.A(poarta_xor_1_out), .B(Cin), .Out(S));
  Poarta_Xor poarta_xor_3 (.A(poarta_not_2_1_out), .B(poarta_not_2_2_out), .Out(Cout));
endmodule
