// Digital circuit Sumator_8_biti.dig as structural Verilog
module Sumator_8_biti (
  input  Cin_p,
  input  [7:0] A,
  input  [7:0] B,
  output [7:0] Out,
  output Cout_p
);

  wire sumator_1_bit_1_cout, sumator_1_bit_2_cout, sumator_1_bit_3_cout, sumator_1_bit_4_cout,
       sumator_1_bit_5_cout, sumator_1_bit_6_cout, sumator_1_bit_7_cout;

  Sumator_1_bit sumator_1_bit_1 (.A(A[0]), .B(B[0]), .Cin(Cin_p), .S(Out[0]), .Cout(sumator_1_bit_1_cout));
  Sumator_1_bit sumator_1_bit_2 (
    .A(A[1]), .B(B[1]), .Cin(sumator_1_bit_1_cout), .S(Out[1]), .Cout(sumator_1_bit_2_cout));
  Sumator_1_bit sumator_1_bit_3 (
    .A(A[2]), .B(B[2]), .Cin(sumator_1_bit_2_cout), .S(Out[2]), .Cout(sumator_1_bit_3_cout));
  Sumator_1_bit sumator_1_bit_4 (
    .A(A[3]), .B(B[3]), .Cin(sumator_1_bit_3_cout), .S(Out[3]), .Cout(sumator_1_bit_4_cout));
  Sumator_1_bit sumator_1_bit_5 (
    .A(A[4]), .B(B[4]), .Cin(sumator_1_bit_4_cout), .S(Out[4]), .Cout(sumator_1_bit_5_cout));
  Sumator_1_bit sumator_1_bit_6 (
    .A(A[5]), .B(B[5]), .Cin(sumator_1_bit_5_cout), .S(Out[5]), .Cout(sumator_1_bit_6_cout));
  Sumator_1_bit sumator_1_bit_7 (
    .A(A[6]), .B(B[6]), .Cin(sumator_1_bit_6_cout), .S(Out[6]), .Cout(sumator_1_bit_7_cout));
  Sumator_1_bit sumator_1_bit_8 (.A(A[7]), .B(B[7]), .Cin(sumator_1_bit_7_cout), .S(Out[7]), .Cout(Cout_p));
endmodule
